# Fritzing sketch 01-Bluetooth-Control (saved by Fritzing 0.9.3b)
breadboards: 1

parts:
  L298N1 = L298N DC motor driver
  M1 = DC Motor  # not connected
  M2 = DC Motor  # not connected
  VCC2 = 4 x AAA Battery Mount
  VCC1 = Battery block 9V  # not connected
  Parça1 = Arduino Uno (Rev3)
  BT1 = Bluetooth HC-06u [package=THT]
  R1 = Resistor [tolerance=±5% resistance=1k package=THT]
  R2 = Resistor [tolerance=±5% resistance=1k package=THT]
  R3 = Resistor [tolerance=±5% resistance=1k package=THT]

nets:
  GND: L298N1.GND, BT1.GND, R1.Pin_1
  N1: L298N1.ENA, Parça1.D5_PWM
  N2: L298N1.ENB, Parça1.D11_PWM/MOSI
  N3: L298N1.IN1, Parça1.D6_PWM
  N4: L298N1.IN2, Parça1.D7
  N5: L298N1.IN3, Parça1.D9_PWM
  N6: L298N1.IN4, Parça1.D10_PWM/SS
  N7: VCC2.-, Parça1.GND
  N8: VCC2.+, Parça1.VIN
  N9: Parça1.D3_PWM, BT1.TXD
  N10: Parça1.D4, R2.Pin_0
  5V: Parça1.5V, BT1.VCC
  N11: BT1.RXD, R2.Pin_1, R3.Pin_0
  N12: R1.Pin_0, R3.Pin_1

custom parts:
  L298N DC motor driver: 2x DC motor driver with 78M05 positive voltage regulator (7..35 V) L298N: max 46 V, 2 A Set 5 V Enable jumper to enable 5 V regultor (needed for the L298N) and +5 V output at screw terminal or supply external +5 V at screw terminal Set ENA and/or ENB to +5 V to enable motor permanently or supply ENA and/or ENB with PWM signal IN1 and IN2 set rotation directory for motor A (OUT1/OUT2) IN2 and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
  Bluetooth HC-06u: Bluetooth HC-06 - face up, pins down 16.5mm x 37.5mm PCB
