# Fritzing sketch 02-Obstacle-Avoidance (saved by Fritzing 0.9.3b)

parts:
  Parça1 = Arduino Uno (Rev3)
  L298N1 = L298N DC motor driver
  M1 = DC Motor  # not connected
  M2 = DC Motor  # not connected
  VCC1 = Battery block 9V
  VCC2 = 4 x AAA Battery Mount
  hc-sr1 = hc-sr04

nets:
  N1: Parça1.D10_PWM/SS, L298N1.ENB
  N2: Parça1.D11_PWM/MOSI, L298N1.IN3
  GND: Parça1.GND, L298N1.GND, VCC1.-, VCC2.-, hc-sr1.GND
  N3: Parça1.D2, hc-sr1.Trig
  N4: Parça1.D3_PWM, hc-sr1.Echo
  N5: Parça1.D4, L298N1.IN4
  N6: Parça1.D5_PWM, L298N1.ENA
  N7: Parça1.D6_PWM, L298N1.IN1
  N8: Parça1.D7, L298N1.IN2
  5V: Parça1.5V, hc-sr1.VCC
  N9: Parça1.VIN, VCC2.+

custom parts:
  L298N DC motor driver: 2x DC motor driver with 78M05 positive voltage regulator (7..35 V) L298N: max 46 V, 2 A Set 5 V Enable jumper to enable 5 V regultor (needed for the L298N) and +5 V output at screw terminal or supply external +5 V at screw terminal Set ENA and/or ENB to +5 V to enable motor permanently or supply ENA and/or ENB with PWM signal IN1 and IN2 set rotation directory for motor A (OUT1/OUT2) IN2 and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
