# Fritzing sketch 03-Parking-Sensor (saved by Fritzing 0.9.3b)
breadboards: 1

parts:
  Parça1 = Arduino Nano (Rev3.0)
  J1 = Piezo Speaker
  hc-sr1 = hc-sr04
  R1 = Resistor [tolerance=±5% resistance=220 package=THT]
  R2 = Resistor [tolerance=±5% resistance=220 package=THT]
  R3 = Resistor [tolerance=±5% resistance=220 package=THT]
  R4 = Resistor [tolerance=±5% resistance=220 package=THT]
  R5 = Resistor [tolerance=±5% resistance=220 package=THT]
  LED1 = LED - 5mm [color="Red (633nm)" package="5 mm [THT]"]
  LED2 = LED - 5mm [color="Yellow (595nm)" package="5 mm [THT]"]
  LED3 = LED - 5mm [color="Green (570nm)" package="5 mm [THT]"]
  LED4 = LED - 5mm [color="Blue (505nm)" package="5 mm [THT]"]
  VCC1 = 4 x AAA Battery Mount

nets:
  GND: Parça1.GND, hc-sr1.GND, R1.Pin_0, R2.Pin_0, R3.Pin_0, R4.Pin_0, R5.Pin_0, VCC1.-
  N1: Parça1.D2, J1.pin2
  N2: Parça1.D3, LED4.anode
  N3: Parça1.D4, LED3.anode
  N4: Parça1.D5, LED2.anode
  N5: Parça1.D6, LED1.anode
  N6: Parça1.VIN, VCC1.+
  5V: Parça1.5V, hc-sr1.VCC
  N7: Parça1.A1, hc-sr1.Echo
  N8: Parça1.A0, hc-sr1.Trig
  N9: J1.pin1, R1.Pin_1
  N10: R2.Pin_1, LED1.cathode
  N11: R3.Pin_1, LED2.cathode
  N12: R4.Pin_1, LED3.cathode
  N13: R5.Pin_1, LED4.cathode
