# Fritzing sketch 04-Integrated-System (saved by Fritzing 0.9.3b)
breadboards: 1

parts:
  L298N1 = L298N DC motor driver
  M1 = DC Motor  # not connected
  M2 = DC Motor  # not connected
  J1 = Piezo Speaker
  Parça2 = Arduino Nano (Rev3.0)
  BT1 = Bluetooth HC-06u [package=THT]
  R1 = Resistor [tolerance=±5% resistance=1k package=THT]
  R2 = Resistor [tolerance=±5% resistance=1k package=THT]
  R3 = Resistor [tolerance=±5% resistance=1k package=THT]
  hc-sr1 = hc-sr04
  VCC1 = Battery block 9V
  VCC2 = 4 x AAA Battery Mount
  R4 = Resistor [tolerance=±5% resistance=220 package=THT]
  hc-sr2 = hc-sr04

nets:
  GND: L298N1.GND, Parça2.GND, R3.Pin_1, hc-sr1.GND, VCC1.-, VCC2.-, R4.Pin_0, hc-sr2.GND
  N1: L298N1.ENA, Parça2.D5
  N2: L298N1.ENB, Parça2.D11/MOSI
  N3: L298N1.IN1, Parça2.D6
  N4: L298N1.IN2, Parça2.D7
  N5: L298N1.IN3, Parça2.D9
  N6: L298N1.IN4, Parça2.D10
  N7: J1.pin1, R4.Pin_1
  N8: J1.pin2, Parça2.D2
  N9: Parça2.D3, BT1.TXD
  N10: Parça2.D4, R1.Pin_0
  N11: Parça2.D8, hc-sr2.Echo
  N12: Parça2.D12/MISO, hc-sr1.Echo
  N13: Parça2.VIN, VCC2.+
  VCC: Parça2.5V, BT1.VCC, hc-sr1.VCC, hc-sr2.VCC
  N14: Parça2.A0, hc-sr2.Trig
  N15: Parça2.D13/SCK, hc-sr1.Trig
  N16: BT1.GND, R2.Pin_1, R3.Pin_0
  N17: BT1.RXD, R1.Pin_1, R2.Pin_0

custom parts:
  L298N DC motor driver: 2x DC motor driver with 78M05 positive voltage regulator (7..35 V) L298N: max 46 V, 2 A Set 5 V Enable jumper to enable 5 V regultor (needed for the L298N) and +5 V output at screw terminal or supply external +5 V at screw terminal Set ENA and/or ENB to +5 V to enable motor permanently or supply ENA and/or ENB with PWM signal IN1 and IN2 set rotation directory for motor A (OUT1/OUT2) IN2 and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
  Bluetooth HC-06u: Bluetooth HC-06 - face up, pins down 16.5mm x 37.5mm PCB
